# Fritzing sketch Houston Headphone Amp 2022 2.1 (saved by Fritzing 0.9.9b)
circuit board: 6.20652cm x 6.68619cm
breadboards: 1

parts:
  4069 = IC, DIP package, 14 pins [chip_label=4069]
  R1 = Resistor [tolerance=±5% resistance=1k power=0.25 package=THT]
  C1 = Ceramic Capacitor [capacitance=10nF package="100 mil [THT, multilayer]"]
  R2 = Resistor [tolerance=±5% resistance=100 power=0.25 package=THT]
  R3 = Resistor [tolerance=±5% resistance=1k power=0.25 package=THT]
  C3 = Ceramic Capacitor [capacitance=10nF package="100 mil [THT, multilayer]"]
  R4 = Resistor [tolerance=±5% resistance=100 power=0.25 package=THT]
  R8 = Rotary Potentiometer (Large) [maximum_resistance=100kΩ package=THT]
  POT = Rotary Potentiometer (Large) [maximum_resistance=100kΩ package=THT]
  IN = female pin header, 3 pins [form="♀ (female)"]
  R10 = Resistor [tolerance=±5% resistance=100 power=0.25 package=THT]
  OUT = female pin header, 3 pins [form="♀ (female)"]
  R11 = Resistor [tolerance=±5% resistance=100k power=0.25 package=THT]
  R12 = Resistor [tolerance=±5% resistance=100k power=0.25 package=THT]
  C5 = Electrolytic Capacitor [capacitance=470µF voltage=35V package="200 mil [THT, electrolytic]"]
  LED1 = LED - 5mm [color="Red (633nm)" current=0.030 package="5 mm [THT]"]
  R13 = Resistor [tolerance=±5% resistance=10k power=0.25 package=THT]
  9V = female pin header, 1 pin [form="♀ (female)"]
  GND = female pin header, 1 pin [form="♀ (female)"]
  C4 = Electrolytic Capacitor [capacitance=220µF voltage=35V package="200 mil [THT, electrolytic]"]
  C3_2 = Electrolytic Capacitor [capacitance=220µF voltage=35V package="200 mil [THT, electrolytic]"]
  J2 = AUDIO-JACK2 [package=audio-jack]
  J3 = AUDIO-JACK2 [package=audio-jack]
  J1 = Power Jack [package=power_jack_slot]
  BATT+ = female pin header, 2 pins [form="♀ (female)"]
  SW1 = female pin header, 3 pins [form="♀ (female)"]
  RCA-R = RCA [package=rca_lock]
  RCA-L = RCA [package=rca_lock]

nets:
  N1: 4069.pin1, 4069.pin3, 4069.pin5, R1.Pin_1, R12.Pin_1
  N2: 4069.pin2, 4069.pin4, 4069.pin6, R2.Pin_0
  N3: 4069.pin7, C1.0, C3.0, R8.leg1, POT.leg1, IN.pin1, OUT.pin1, C5.-, LED1.cathode, GND.pin1, J2.SLEEVE, J3.SLEEVE, J1.PWR, BATT+.pin2, RCA-R.SHELL, RCA-L.SHELL
  N4: 4069.pin8, 4069.pin10, 4069.pin12, R4.Pin_0
  N5: 4069.pin9, 4069.pin11, 4069.pin13, R3.Pin_1, R11.Pin_1
  N6: 4069.pin14, R10.Pin_1, R11.Pin_0, R12.Pin_0, C5.+, R13.Pin_1
  N7: R1.Pin_0, IN.pin2, J2.TIP
  N8: C1.1, R2.Pin_1, C4.+
  N9: R3.Pin_0, IN.pin3, J2.RING
  N10: C3.1, R4.Pin_1, C3_2.+
  N11: R8.wiper, OUT.pin3, J3.RING
  N12: R8.leg2, C3_2.-
  N13: POT.wiper, OUT.pin2, J3.TIP
  N14: POT.leg2, C4.-
  N15: R10.Pin_0, 9V.pin1, SW1.pin2
  N16: LED1.anode, R13.Pin_0
  N17: J3.RSH, RCA-R.PIN, RCA-R.SWITCH
  N18: J3.TSH, RCA-L.PIN, RCA-L.SWITCH
  N19: J1.GNDBREAK, SW1.pin1
  N20: J1.GND, BATT+.pin1

notes:
  SNORKEL 2015
  INVERT-A-BIT
  LEFT
  RIGHT
  GND
  R
  L
  G
  Rev 2022 skate323k137
  9V DC IN
  TI-Calc
  PHONES
  CENTER NEGATIVE
  POWER SW
  For HoustonTracker2
  Mount Optional
  RCA Jacks
  on underside
  TP1
  TP2
  IN
