# Fritzing sketch Houston Headphone amp 3 (saved by Fritzing 0.9.2b)
circuit board: 4.2cm x 5.4cm
breadboards: 1

parts:
  4069 = IC, DIP package, 14 pins [chip_label=4069]
  R1 = Resistor [tolerance=±5% resistance=1k package=THT]
  C1 = Ceramic Capacitor [capacitance=10nF package="100 mil [THT, multilayer]"]
  R2 = Resistor [tolerance=±5% resistance=100 package=THT]
  R3 = Resistor [tolerance=±5% resistance=1k package=THT]
  C3 = Ceramic Capacitor [capacitance=10nF package="100 mil [THT, multilayer]"]
  R4 = Resistor [tolerance=±5% resistance=100 package=THT]
  R8 = Rotary Potentiometer (Large) [maximum_resistance=100kΩ package=THT]
  POT = Rotary Potentiometer (Large) [maximum_resistance=100kΩ package=THT]
  IN = female pin header, 3 pins [form="♀ (female)"]
  R10 = Resistor [tolerance=±5% resistance=100 package=THT]
  OUT = female pin header, 3 pins [form="♀ (female)"]
  R11 = Resistor [tolerance=±5% resistance=100k package=THT]
  R12 = Resistor [tolerance=±5% resistance=100k package=THT]
  C5 = Electrolytic Capacitor [capacitance=470µF voltage=35V package="200 mil [THT, electrolytic]"]
  LED1 = LED - 5mm [color="Red (633nm)" package="5 mm [THT]"]
  R13 = Resistor [tolerance=±5% resistance=10k package=THT]
  9V = female pin header, 1 pin [form="♀ (female)"]
  GND = female pin header, 1 pin [form="♀ (female)"]
  C4 = Electrolytic Capacitor [capacitance=220µF voltage=35V package="200 mil [THT, electrolytic]"]
  C3_2 = Electrolytic Capacitor [capacitance=220µF voltage=35V package="200 mil [THT, electrolytic]"]

nets:
  N1: 4069.pin1, 4069.pin3, 4069.pin5, R1.Pin_1, R12.Pin_1
  N2: 4069.pin2, 4069.pin4, 4069.pin6, R2.Pin_0
  N3: 4069.pin7, C1.0, C3.0, R8.leg1, POT.leg1, IN.pin1, OUT.pin1, C5.-, LED1.cathode, GND.pin1
  N4: 4069.pin8, 4069.pin10, 4069.pin12, R4.Pin_0
  N5: 4069.pin9, 4069.pin11, 4069.pin13, R3.Pin_1, R11.Pin_1
  N6: 4069.pin14, R10.Pin_1, R11.Pin_0, R12.Pin_0, C5.+, R13.Pin_1
  N7: R1.Pin_0, IN.pin2
  N8: C1.1, R2.Pin_1, C4.+
  N9: R3.Pin_0, IN.pin3
  N10: C3.1, R4.Pin_1, C3_2.+
  N11: R8.wiper, OUT.pin3
  N12: R8.leg2, C3_2.-
  N13: POT.wiper, OUT.pin2
  N14: POT.leg2, C4.-
  N15: R10.Pin_0, 9V.pin1
  N16: LED1.anode, R13.Pin_0

notes:
  SNORKEL 2015
  INVERT-A-BIT
  LEFT
  RIGHT
  GND
  R
  L
  G
